# Fritzing sketch Ziafati_PoorBehzad_Button_ON_OFF_in_Serial_Monitor (saved by Fritzing 0.9.4)
breadboards: 1

parts:
  Part1 = Arduino Uno (Rev3)
  LED1 = LED - 5mm [color="Red (633nm)" package="5 mm [THT]"]

nets:
  N1: Part1.D13/SCK, LED1.anode
  N2: Part1.GND, LED1.cathode

notes:
  ضیافتی_پوربهزاد
  پروژه دکمه ON,OFF
  در Serial Monitor
