# Fritzing sketch Ziafati_PoorBehzad_Tas (saved by Fritzing 0.9.4)
breadboards: 1

parts:
  Part1 = Arduino Uno (Rev3)
  LED1 = LED - 5mm [color="Red (633nm)" package="5 mm [THT]"]
  LED2 = LED - 5mm [color="Red (633nm)" package="5 mm [THT]"]
  LED3 = LED - 5mm [color="Red (633nm)" package="5 mm [THT]"]
  LED4 = LED - 5mm [color="Red (633nm)" package="5 mm [THT]"]
  LED5 = LED - 5mm [color="Red (633nm)" package="5 mm [THT]"]
  LED6 = LED - 5mm [color="Red (633nm)" package="5 mm [THT]"]
  S1 = Pushbutton [package="[THT]"]
  R1 = Resistor [tolerance=±5% resistance=220 package=THT]

nets:
  N1: Part1.D2, LED3.anode
  N2: Part1.D3_PWM, LED2.anode
  N3: Part1.D4, LED1.anode
  N4: Part1.D5_PWM, LED5.anode
  N5: Part1.D6_PWM, LED4.anode
  N6: Part1.D7, LED6.anode
  N7: Part1.RESET, S1.Pin_1, S1.Pin_2
  N8: Part1.GND, LED1.cathode, LED2.cathode, LED3.cathode, LED4.cathode, LED5.cathode, LED6.cathode, R1.Pin_1
  N9: S1.Pin_3, S1.Pin_4, R1.Pin_0

notes:
  ضیافتی_پوربهزاد
  پروژه تاس
